# Fritzing sketch LCD Display (saved by Fritzing 0.6.5b)
breadboards: 1

parts:
  LCD1 = LCD screen
  R1 = Rotary Potentiometer (Small) [maximum_resistance=100kΩ]
  Arduino1 = Arduino

nets:
  VSS: LCD1.VSS, LCD1.R/W, LCD1.LED-, R1.leg1, Arduino1.GND
  VDD: LCD1.VDD, LCD1.LED+, R1.leg2, Arduino1.+5V
  N1: LCD1.V0, R1.wiper
  N2: LCD1.RS, Arduino1.D2
  N3: LCD1.E, Arduino1.D3
  N4: LCD1.DB4, Arduino1.D4
  N5: LCD1.DB5, Arduino1.D5
  N6: LCD1.DB6, Arduino1.D6
  N7: LCD1.DB7, Arduino1.D7
